# Fritzing sketch AirQuality (saved by Fritzing 0.9.4)
breadboards: 1

parts:
  Part1 = Arduino Uno (Rev3)
  U1 = ESP8266 WiFi Module [part_number=ESP8266]
  Part2 = MQ-4
  Part3 = MQ-4
  U2 = Sharp Dust Sensor [part_number=GP2Y1010AU0F]
  R1 = Resistor [tolerance=±5% resistance=220 package=THT]
  C1 = Capacitor Polarized [package=cpol-radial-1000uf-25v]

nets:
  N1: Part1.A0, Part2.AO
  N2: Part1.A1, Part3.AO
  N3: Part1.A5/SCL, U2.Vo
  N4: Part1.D10_PWM/SS, U1.TXD
  N5: Part1.D11_PWM/MOSI, U1.RXD
  GND: Part1.GND, U1.GND, Part2.GND, Part3.GND, U2.S-GND
  N6: Part1.D7, U2.LED
  VCC: Part1.3V3, U1.VCC, U1.CH_PD, Part2.VCC, Part3.VCC
  5V: Part1.5V, U2.VCC, R1.Pin_0, C1.+
  N7: U2.V-LED, R1.Pin_1
  N8: U2.LED-GND, C1.-

notes:
  MQ-135

custom parts:
  ESP8266 WiFi Module: Generic WiFi Module based on the ESP8266 with onboard PCB antenna and UART communications
  Sharp Dust Sensor: Sharp GP2Y1010AU0F Dust Sensor
